// Digital circuit 1bitFullAdder.dig as structural Verilog
module _1bitFullAdder (
  input  A,
  input  B,
  input  Carryin,
  output Carryout,
  output Sum
);

  wire and_1_out, and_2_out, xor_1_out;

  xor xor_1 (xor_1_out, A, B);
  xor xor_2 (Sum, xor_1_out, Carryin);
  and and_1 (and_1_out, Carryin, xor_1_out);
  and and_2 (and_2_out, B, A);
  or or_1 (Carryout, and_1_out, and_2_out);
endmodule
