// Digital circuit 2BitMultiplier.dig as structural Verilog
module _2BitMultiplier (
  input  A1,
  input  A0,
  input  B1,
  input  B0,
  output P3,
  output P2,
  output P1,
  output P0
);

  wire and_2_out, and_3_out, and_4_out, and_5_out, and_6_out, and_7_out, not_1_out, not_2_out, not_3_out,
       not_4_out, not_5_out, not_6_out, or_2_out, or_3_out;

  not not_1 (not_1_out, A0);
  not not_2 (not_2_out, B0);
  not not_3 (not_3_out, A1);
  not not_4 (not_4_out, A0);
  not not_5 (not_5_out, B1);
  not not_6 (not_6_out, B0);
  and and_1 (P3, A1, A0, B1, B0);
  and and_2 (and_2_out, A1, not_1_out, B1);
  and and_3 (and_3_out, B1, not_2_out, A1);
  and and_4 (and_4_out, not_3_out, A0, B1);
  and and_5 (and_5_out, A1, not_4_out, B0);
  and and_6 (and_6_out, not_5_out, B0, A1);
  and and_7 (and_7_out, B1, not_6_out, A0);
  and and_8 (P0, A0, B0);
  or or_1 (P2, and_2_out, and_3_out);
  or or_2 (or_2_out, and_4_out, and_5_out);
  or or_3 (or_3_out, and_6_out, and_7_out);
  or or_4 (P1, or_2_out, or_3_out);
endmodule
