// Digital circuit 4bitRippleCarry.dig as structural Verilog
module _4bitRippleCarry (
  input  B0,
  input  A3,
  input  B3,
  input  A1,
  input  B1,
  input  A2,
  input  A0,
  input  Cin,
  input  B2,
  output Sum0,
  output Sum1,
  output Sum2,
  output Sum3,
  output Cout
);

  wire _1bitfulladder_1_carryout, _1bitfulladder_2_carryout, _1bitfulladder_3_carryout;

  _1bitFullAdder _1bitfulladder_1 (.A(A0), .B(B0), .Carryin(Cin), .Carryout(_1bitfulladder_1_carryout), .Sum(Sum0));
  _1bitFullAdder _1bitfulladder_2 (
    .A(A1), .B(B1), .Carryin(_1bitfulladder_1_carryout), .Carryout(_1bitfulladder_2_carryout), .Sum(Sum1));
  _1bitFullAdder _1bitfulladder_3 (
    .A(A2), .B(B2), .Carryin(_1bitfulladder_2_carryout), .Carryout(_1bitfulladder_3_carryout), .Sum(Sum2));
  _1bitFullAdder _1bitfulladder_4 (.A(A3), .B(B3), .Carryin(_1bitfulladder_3_carryout), .Carryout(Cout), .Sum(Sum3));
endmodule
